# Fritzing sketch raspberry-pi-wire-schematics (saved by Fritzing 0.9.4)

parts:
  Raspberry_Pi_1 = Raspberry Pi 3 [part_number=RPI-3-V1.2]
  J1 = Basic Servo

nets:
  GND: Raspberry_Pi_1.GND, J1.gnd
  N1: Raspberry_Pi_1.GPIO17, J1.pulse
  5V: Raspberry_Pi_1.5V, J1.vcc
